# Fritzing sketch turntable (saved by Fritzing 0.9.2b)
breadboards: 1

parts:
  M1 = DC Motor
  D1 = Zener Diode [part_number=1N4732A breakdown_voltage=3.6V package="300 mil [THT]"]
  R1 = Resistor [tolerance=±5% resistance=1k package=THT]
  Q1 = NPN-Transistor [package="SOT-23 [SMD]"]
  Part1 = Arduino Leonardo (Rev3b)
  J6 = Power Jack [package=power_jack_smd]
  R2 = Rotary Potentiometer (Small) [maximum_resistance=100kΩ package=THT]

nets:
  N1: M1.pin_1, D1.cathode
  N2: M1.pin_2, J6.PWR
  N3: D1.anode, Q1.1
  N4: R1.Pin_0, Q1.0
  GND: Q1.2, Part1.GND, J6.GND, R2.leg1
  N5: Part1.5V, R2.leg2
  N6: Part1.A0, R2.wiper
